# Fritzing sketch Lecture_etat_interrupteur (saved by Fritzing 0.9.1b)
breadboards: 1

parts:
  Composant1 = Arduino Mega 2560 (Rev3)
  S1 = Pushbutton [package=THT]
  S2 = Pushbutton [package=THT]
  S3 = Pushbutton [package=THT]

nets:
  N1: Composant1.D50, S1.leg1
  N2: Composant1.D51, S2.leg1
  N3: Composant1.D52, S3.leg1
  N4: Composant1.GND, S1.leg0, S2.leg0, S3.leg0
